# Fritzing sketch routetest (saved by Fritzing 0.9.3b)
circuit board: 8.46667cm x 5.64444cm
breadboards: 1

parts:
  パーツ1 = LilyPad Coin Cell Battery Holder
  パーツ2 = LilyPad LED
  パーツ3 = LilyPad LED
  パーツ4 = LilyPad LED

nets:
  N1: パーツ1.-, パーツ2.+, パーツ2.-, パーツ3.+, パーツ3.-, パーツ4.+, パーツ4.-
